// Logisim project 交通控制灯.circ as structural Verilog: 8 circuits, main circuit 红绿灯
module \计数器  (
  input  [3:0] Din,
  input  \异步置位 ,
  input  CLK,
  input  \使能 ,
  input  \Mode_为1时倒计时 ,
  output [3:0] Q,
  output \cout_进位 
);

  wire D0, D1, D2, D3, not_1_out, not_2_out, not_3_out, not_4_out, \状态转换_1_n0 , \状态转换_1_n1 , \状态转换_1_n2 ,
       \状态转换_1_n3 ;

  \状态转换  \u_状态转换_1  (
    .S0(Q[0]), .S1(Q[1]), .S2(Q[2]), .S3(Q[3]), .Mode(\Mode_为1时倒计时 ), .N3(\状态转换_1_n3 ), .N2(\状态转换_1_n2 ),
    .N1(\状态转换_1_n1 ), .N0(\状态转换_1_n0 ));
  D_Flip_Flop #(.trigger("rising"), .Pre_Clr_Positions("LEGACY"), .NegatePresetClear("false"), .enable("true"), .NewFFLayout("false")) d_ff_1 (
    .clk(CLK), .D(\状态转换_1_n3 ), .Q(Q[3]), .preset(D0), .en(\使能 ), .reset(not_1_out));  // open: Qn
  D_Flip_Flop #(.trigger("rising"), .Pre_Clr_Positions("LEGACY"), .NegatePresetClear("false"), .enable("true"), .NewFFLayout("false")) d_ff_2 (
    .clk(CLK), .D(\状态转换_1_n1 ), .Q(Q[1]), .preset(D2), .en(\使能 ), .reset(not_3_out));  // open: Qn
  D_Flip_Flop #(.trigger("rising"), .Pre_Clr_Positions("LEGACY"), .NegatePresetClear("false"), .enable("true"), .NewFFLayout("false")) d_ff_3 (
    .clk(CLK), .D(\状态转换_1_n0 ), .Q(Q[0]), .preset(D3), .en(\使能 ), .reset(not_4_out));  // open: Qn
  D_Flip_Flop #(.trigger("rising"), .Pre_Clr_Positions("LEGACY"), .NegatePresetClear("false"), .enable("true"), .NewFFLayout("false")) d_ff_4 (
    .clk(CLK), .D(\状态转换_1_n2 ), .Q(Q[2]), .preset(D1), .en(\使能 ), .reset(not_2_out));  // open: Qn
  not not_1 (not_1_out, D0);
  not not_2 (not_2_out, D1);
  not not_3 (not_3_out, D2);
  not not_4 (not_4_out, D3);
  \输出函数  \u_输出函数_1  (.S1(Q[3]), .S2(Q[2]), .S3(Q[1]), .S4(Q[0]), .mode(\Mode_为1时倒计时 ), .cout(\cout_进位 ));
  assign {D0, D1, D2, D3} = \异步置位  ? Din : 4'bz;  // Controlled_Buffer controlled_buffer_1

  // Other names for the same wires on the sheet: enable = \使能 ; Mode = \Mode_为1时倒计时 
endmodule

module \输出函数  (
  input  S1,
  input  S2,
  input  S3,
  input  S4,
  input  mode,
  output cout
);

  wire and_1_out, and_2_out, not_1_out, not_2_out, not_3_out, not_4_out, not_5_out, not_6_out, not_7_out;

  not not_1 (not_1_out, S3);
  not not_2 (not_2_out, S2);
  not not_3 (not_3_out, mode);
  not not_4 (not_4_out, S4);
  not not_5 (not_5_out, S3);
  not not_6 (not_6_out, S2);
  not not_7 (not_7_out, S1);
  and and_1 (and_1_out, S4, not_1_out, not_2_out, S1, not_3_out);
  and and_2 (and_2_out, not_4_out, not_5_out, not_6_out, not_7_out, mode);
  or or_1 (cout, and_1_out, and_2_out);
endmodule

module \状态转换  (
  input  S0,
  input  S1,
  input  S2,
  input  S3,
  input  Mode,
  output N3,
  output N2,
  output N1,
  output N0
);

  wire and_1_out, and_2_out, and_3_out, and_4_out, and_5_out, and_6_out, and_7_out, and_8_out, and_9_out,
       and_10_out, and_11_out, and_12_out, and_13_out, and_14_out, and_15_out, and_16_out, and_17_out,
       and_18_out, and_19_out, and_20_out, and_21_out, and_22_out, and_23_out, and_24_out, and_25_out,
       and_26_out, and_27_out, and_28_out, and_29_out, and_30_out, not_1_out, not_2_out, not_3_out,
       not_4_out, not_5_out, not_6_out, not_7_out, not_8_out, not_9_out, not_10_out, not_11_out, not_12_out,
       not_13_out, not_14_out, not_15_out, not_16_out, not_17_out, not_18_out, not_19_out, not_20_out,
       not_21_out, not_22_out, not_23_out, not_24_out, not_25_out, not_26_out, not_27_out, not_28_out,
       not_29_out, not_30_out, not_31_out, not_32_out, not_33_out, not_34_out, not_35_out, not_36_out,
       not_37_out, not_38_out, not_39_out, not_40_out, not_41_out, not_42_out, not_43_out, not_44_out,
       not_45_out, not_46_out, not_47_out, not_48_out, not_49_out, not_50_out, not_51_out, not_52_out,
       not_53_out, not_54_out, not_55_out, not_56_out, not_57_out, not_58_out, not_59_out, not_60_out,
       not_61_out, not_62_out, not_63_out, not_64_out, not_65_out, not_66_out, not_67_out, not_68_out,
       not_69_out, not_70_out, not_71_out, not_72_out, not_73_out, not_74_out, not_75_out, not_76_out,
       not_77_out, not_78_out, not_79_out, not_80_out, not_81_out, not_82_out, not_83_out, not_84_out,
       not_85_out, not_86_out, not_87_out, not_88_out, not_89_out, not_90_out, not_91_out;

  not not_1 (not_1_out, S3);
  not not_2 (not_2_out, Mode);
  not not_3 (not_3_out, S2);
  not not_4 (not_4_out, S1);
  not not_5 (not_5_out, S0);
  not not_6 (not_6_out, Mode);
  not not_7 (not_7_out, S2);
  not not_8 (not_8_out, S1);
  not not_9 (not_9_out, S3);
  not not_10 (not_10_out, S2);
  not not_11 (not_11_out, S1);
  not not_12 (not_12_out, S0);
  not not_13 (not_13_out, S3);
  not not_14 (not_14_out, S2);
  not not_15 (not_15_out, Mode);
  not not_16 (not_16_out, S3);
  not not_17 (not_17_out, S1);
  not not_18 (not_18_out, S0);
  not not_19 (not_19_out, Mode);
  not not_20 (not_20_out, S3);
  not not_21 (not_21_out, S1);
  not not_22 (not_22_out, Mode);
  not not_23 (not_23_out, S3);
  not not_24 (not_24_out, S0);
  not not_25 (not_25_out, Mode);
  not not_26 (not_26_out, S2);
  not not_27 (not_27_out, S1);
  not not_28 (not_28_out, S0);
  not not_29 (not_29_out, S3);
  not not_30 (not_30_out, S3);
  not not_31 (not_31_out, S0);
  not not_32 (not_32_out, S3);
  not not_33 (not_33_out, S1);
  not not_34 (not_34_out, S3);
  not not_35 (not_35_out, S2);
  not not_36 (not_36_out, S1);
  not not_37 (not_37_out, Mode);
  not not_38 (not_38_out, S3);
  not not_39 (not_39_out, S2);
  not not_40 (not_40_out, S0);
  not not_41 (not_41_out, Mode);
  not not_42 (not_42_out, S3);
  not not_43 (not_43_out, S1);
  not not_44 (not_44_out, Mode);
  not not_45 (not_45_out, S3);
  not not_46 (not_46_out, S0);
  not not_47 (not_47_out, Mode);
  not not_48 (not_48_out, S2);
  not not_49 (not_49_out, S1);
  not not_50 (not_50_out, S0);
  not not_51 (not_51_out, S3);
  not not_52 (not_52_out, S3);
  not not_53 (not_53_out, S1);
  not not_54 (not_54_out, S0);
  not not_55 (not_55_out, S3);
  not not_56 (not_56_out, S2);
  not not_57 (not_57_out, S3);
  not not_58 (not_58_out, S2);
  not not_59 (not_59_out, S1);
  not not_60 (not_60_out, S0);
  not not_61 (not_61_out, Mode);
  not not_62 (not_62_out, S3);
  not not_63 (not_63_out, S2);
  not not_64 (not_64_out, S0);
  not not_65 (not_65_out, Mode);
  not not_66 (not_66_out, S3);
  not not_67 (not_67_out, S1);
  not not_68 (not_68_out, S0);
  not not_69 (not_69_out, Mode);
  not not_70 (not_70_out, S3);
  not not_71 (not_71_out, S0);
  not not_72 (not_72_out, Mode);
  not not_73 (not_73_out, S2);
  not not_74 (not_74_out, S1);
  not not_75 (not_75_out, S0);
  not not_76 (not_76_out, Mode);
  not not_77 (not_77_out, S2);
  not not_78 (not_78_out, S1);
  not not_79 (not_79_out, S0);
  not not_80 (not_80_out, S3);
  not not_81 (not_81_out, S0);
  not not_82 (not_82_out, S3);
  not not_83 (not_83_out, S1);
  not not_84 (not_84_out, S0);
  not not_85 (not_85_out, S3);
  not not_86 (not_86_out, S2);
  not not_87 (not_87_out, S0);
  not not_88 (not_88_out, S3);
  not not_89 (not_89_out, S2);
  not not_90 (not_90_out, S1);
  not not_91 (not_91_out, S0);
  and and_1 (and_1_out, not_1_out, S2, S1, S0, not_2_out);
  and and_2 (and_2_out, S3, not_3_out, not_4_out, not_5_out, not_6_out);
  and and_3 (and_3_out, S3, not_7_out, not_8_out, S0, Mode);
  and and_4 (and_4_out, not_9_out, not_10_out, not_11_out, not_12_out, Mode);
  and and_5 (and_5_out, not_13_out, not_14_out, S1, S0, not_15_out);
  and and_6 (and_6_out, not_16_out, S2, not_17_out, not_18_out, not_19_out);
  and and_7 (and_7_out, not_20_out, S2, not_21_out, S0, not_22_out);
  and and_8 (and_8_out, not_23_out, S2, S1, not_24_out, not_25_out);
  and and_9 (and_9_out, S3, not_26_out, not_27_out, not_28_out, Mode);
  and and_10 (and_10_out, not_29_out, S2, S1, S0, Mode);
  and and_11 (and_11_out, not_30_out, S2, S1, not_31_out, Mode);
  and and_12 (and_12_out, not_32_out, S2, not_33_out, S0, Mode);
  and and_13 (and_13_out, not_34_out, not_35_out, not_36_out, S0, not_37_out);
  and and_14 (and_14_out, not_38_out, not_39_out, S1, not_40_out, not_41_out);
  and and_15 (and_15_out, not_42_out, S2, not_43_out, S0, not_44_out);
  and and_16 (and_16_out, not_45_out, S2, S1, not_46_out, not_47_out);
  and and_17 (and_17_out, S3, not_48_out, not_49_out, not_50_out, Mode);
  and and_18 (and_18_out, not_51_out, S2, S1, S0, Mode);
  and and_19 (and_19_out, not_52_out, S2, not_53_out, not_54_out, Mode);
  and and_20 (and_20_out, not_55_out, not_56_out, S1, S0, Mode);
  and and_21 (and_21_out, not_57_out, not_58_out, not_59_out, not_60_out, not_61_out);
  and and_22 (and_22_out, not_62_out, not_63_out, S1, not_64_out, not_65_out);
  and and_23 (and_23_out, not_66_out, S2, not_67_out, not_68_out, not_69_out);
  and and_24 (and_24_out, not_70_out, S2, S1, not_71_out, not_72_out);
  and and_25 (and_25_out, S3, not_73_out, not_74_out, not_75_out, not_76_out);
  and and_26 (and_26_out, S3, not_77_out, not_78_out, not_79_out, Mode);
  and and_27 (and_27_out, not_80_out, S2, S1, not_81_out, Mode);
  and and_28 (and_28_out, not_82_out, S2, not_83_out, not_84_out, Mode);
  and and_29 (and_29_out, not_85_out, not_86_out, S1, not_87_out, Mode);
  and and_30 (and_30_out, not_88_out, not_89_out, not_90_out, not_91_out, Mode);
  or or_1 (N3, and_1_out, and_2_out, and_3_out, and_4_out);
  or or_2 (N2, and_5_out, and_6_out, and_7_out, and_8_out, and_9_out, and_10_out, and_11_out, and_12_out);
  or or_3 (N1, and_13_out, and_14_out, and_15_out, and_16_out, and_17_out, and_18_out, and_19_out, and_20_out);
  or or_4 (N0, and_21_out, and_22_out, and_23_out, and_24_out, and_25_out, and_26_out, and_27_out, and_28_out, and_29_out, and_30_out);
endmodule

// 计数器
module \双位计数器  (
  input  [7:0] in_1,
  input  CLK,
  input  enable,
  input  mode,
  input  \异步置位 ,
  output cout,
  output [7:0] Q
);

  wire not_1_out, \计数器_1_cout_进位 , \计数器_2_cout_进位 ;

  not not_1 (not_1_out, \计数器_2_cout_进位 );
  \计数器  \u_计数器_1  (
    .\Mode_为1时倒计时 (mode), .Q(Q[7:4]), .Din(in_1[7:4]), .\异步置位 (\异步置位 ), .\cout_进位 (\计数器_1_cout_进位 ),
    .CLK(not_1_out), .\使能 (enable));
  Hex_Digit_Display hex_digit_display_1 (.value(Q[3:0]));  // open: dp
  Hex_Digit_Display hex_digit_display_2 (.value(Q[7:4]));  // open: dp
  \计数器  \u_计数器_2  (
    .\Mode_为1时倒计时 (mode), .Q(Q[3:0]), .Din(in_1[3:0]), .\异步置位 (\异步置位 ), .\cout_进位 (\计数器_2_cout_进位 ),
    .CLK(CLK), .\使能 (enable));
  and and_1 (cout, \计数器_2_cout_进位 , \计数器_1_cout_进位 );

  // Other names for the same wires on the sheet: Din[7:0] = in_1; Din2[3:0] = in_1[3:0]; Din1[3:0] = in_1[7:4]
endmodule

// 状态机
module \红绿灯状态机  (
  input  S0,
  input  S1,
  input  S2,
  input  stop,
  output R1,
  output Y1,
  output G1,
  output R2,
  output Y2,
  output G2,
  output Pass1,
  output Pass2
);

  wire and_1_out, and_2_out, and_3_out, and_4_out, not_1_out, not_2_out, not_3_out, not_4_out, not_5_out,
       not_6_out, not_7_out, not_8_out, not_9_out, not_10_out, not_11_out, not_12_out, not_13_out,
       not_14_out, not_15_out, not_16_out, not_17_out, not_18_out, not_19_out, not_20_out, not_21_out,
       not_22_out, not_23_out;

  not not_1 (not_1_out, S0);
  and and_1 (and_1_out, not_1_out, not_2_out, S2);
  not not_2 (not_2_out, S1);
  and and_2 (and_2_out, S1, not_3_out);
  not not_3 (not_3_out, S2);
  not not_4 (not_4_out, S1);
  not not_5 (not_5_out, S2);
  not not_6 (not_6_out, stop);
  not not_7 (not_7_out, S0);
  not not_8 (not_8_out, S1);
  not not_9 (not_9_out, S2);
  not not_10 (not_10_out, stop);
  not not_11 (not_11_out, S0);
  and and_3 (and_3_out, not_11_out, not_12_out);
  not not_12 (not_12_out, S1);
  not not_13 (not_13_out, S1);
  and and_4 (and_4_out, not_13_out, not_14_out);
  not not_14 (not_14_out, S2);
  not not_15 (not_15_out, S2);
  not not_16 (not_16_out, stop);
  not not_17 (not_17_out, S0);
  not not_18 (not_18_out, S2);
  not not_19 (not_19_out, stop);
  not not_20 (not_20_out, S1);
  not not_21 (not_21_out, S2);
  and and_5 (Pass1, not_20_out, not_21_out, not_22_out);
  not not_22 (not_22_out, stop);
  and and_6 (Pass2, S1, not_23_out);
  not not_23 (not_23_out, S2);
  or or_1 (R1, stop, and_1_out, and_2_out);
  and and_7 (Y1, S0, not_4_out, not_5_out, not_6_out);
  and and_8 (G1, not_7_out, not_8_out, not_9_out, not_10_out);
  or or_2 (R2, and_3_out, and_4_out, stop);
  and and_9 (Y2, S0, S1, not_15_out, not_16_out);
  and and_10 (G2, not_17_out, S1, not_18_out, not_19_out);
endmodule

// 生成函数
module \红绿灯生成函数  (
  input  S2,
  input  S1,
  input  S0,
  input  T1,
  input  T2,
  input  T3,
  input  T4,
  input  EMERG,
  output N0,
  output N1,
  output N2
);

  wire and_1_out, and_2_out, and_3_out, and_4_out, and_5_out, and_6_out, and_7_out, and_8_out, and_9_out,
       and_10_out, and_11_out, and_12_out, and_13_out, not_1_out, not_2_out, not_3_out, not_4_out, not_5_out,
       not_6_out, not_7_out, not_8_out, not_9_out, not_10_out, not_11_out, not_12_out, not_13_out,
       not_14_out, not_15_out, not_16_out, not_17_out, not_18_out, not_19_out, not_20_out, not_21_out,
       not_22_out, not_23_out, not_24_out, not_25_out, not_26_out, not_27_out, not_28_out, not_29_out,
       not_30_out, not_31_out, not_32_out, not_33_out, not_34_out, not_35_out, not_36_out, not_37_out;

  not not_1 (not_1_out, S2);
  not not_2 (not_2_out, S1);
  not not_3 (not_3_out, S0);
  not not_4 (not_4_out, S2);
  not not_5 (not_5_out, S1);
  not not_6 (not_6_out, S2);
  not not_7 (not_7_out, S0);
  not not_8 (not_8_out, S2);
  not not_9 (not_9_out, S1);
  not not_10 (not_10_out, S0);
  not not_11 (not_11_out, S2);
  not not_12 (not_12_out, S1);
  not not_13 (not_13_out, EMERG);
  not not_14 (not_14_out, S2);
  not not_15 (not_15_out, S0);
  not not_16 (not_16_out, EMERG);
  not not_17 (not_17_out, S2);
  not not_18 (not_18_out, S0);
  not not_19 (not_19_out, T3);
  not not_20 (not_20_out, EMERG);
  not not_21 (not_21_out, S2);
  not not_22 (not_22_out, T4);
  not not_23 (not_23_out, EMERG);
  not not_24 (not_24_out, S2);
  not not_25 (not_25_out, S1);
  not not_26 (not_26_out, S0);
  not not_27 (not_27_out, EMERG);
  not not_28 (not_28_out, S2);
  not not_29 (not_29_out, S0);
  not not_30 (not_30_out, EMERG);
  not not_31 (not_31_out, S2);
  not not_32 (not_32_out, S1);
  not not_33 (not_33_out, T2);
  not not_34 (not_34_out, EMERG);
  not not_35 (not_35_out, S2);
  not not_36 (not_36_out, T4);
  not not_37 (not_37_out, EMERG);
  and and_1 (and_1_out, not_1_out, not_2_out, not_3_out, EMERG);
  and and_2 (and_2_out, not_4_out, not_5_out, S0, EMERG);
  and and_3 (and_3_out, not_6_out, S1, not_7_out, EMERG);
  and and_4 (and_4_out, not_8_out, S1, S0, EMERG);
  and and_5 (and_5_out, S2, not_9_out, not_10_out, EMERG);
  and and_6 (and_6_out, not_11_out, not_12_out, S0, T2, not_13_out);
  and and_7 (and_7_out, not_14_out, S1, not_15_out, T3, not_16_out);
  and and_8 (and_8_out, not_17_out, S1, not_18_out, not_19_out, not_20_out);
  and and_9 (and_9_out, not_21_out, S1, S0, not_22_out, not_23_out);
  and and_10 (and_10_out, not_24_out, not_25_out, not_26_out, T1, not_27_out);
  and and_11 (and_11_out, not_28_out, S1, not_29_out, T3, not_30_out);
  and and_12 (and_12_out, not_31_out, not_32_out, S0, not_33_out, not_34_out);
  and and_13 (and_13_out, not_35_out, S1, S0, not_36_out, not_37_out);
  or or_1 (N0, and_1_out, and_2_out, and_3_out, and_4_out, and_5_out);
  or or_2 (N1, and_6_out, and_7_out, and_8_out, and_9_out);
  or or_3 (N2, and_10_out, and_11_out, and_12_out, and_13_out);
endmodule

module \红绿灯  (
  input  E,
  input  in_2
);

  wire CLK, dipswitch_1_p1, emerge, G1, G2, not_1_out, not_3_out, or_1_out, or_2_out, Pass1, Pass2, R1, R2,
       RST, T1, T2, T3, T4, xnor_1_out, xnor_2_out, Y1, Y2, YL1, YL2, \暂停 ;
  wire [2:0] STATUS, \红绿灯生成函数_1_n0 ;
  wire [3:0] Dout1, Dout2;
  wire [7:0] time1, time2;
  wire [24:0] LR, LR1;

  LED #(.active("true")) led_1 (.in(R1));
  LED #(.active("true")) led_2 (.in(YL1));
  LED #(.active("true")) led_3 (.in(G1));
  DotMatrix #(.inputtype("column"), .matrixcols(5), .matrixrows(5), .persist(0), .dotshape("square")) dotmatrix_1 (
    .col0(LR[24:20]), .col1(LR[19:15]), .col2(LR[14:10]), .col3(LR[9:5]), .col4(LR[4:0]));
  Register #(.width(3), .trigger("rising"), .Select("low")) register_1 (
    .D(\红绿灯生成函数_1_n0 ), .Q(STATUS), .clk(CLK));  // open: en, clr
  or or_1 (or_1_out, RST, T4);
  Hex_Digit_Display hex_digit_display_1 (.value(Dout1));  // open: dp
  Hex_Digit_Display hex_digit_display_2 (.value(Dout2));  // open: dp
  not not_1 (not_1_out, \暂停 );
  \双位计数器  \u_双位计数器_1  (
    .enable(\暂停 ), .mode(1'b1), .\异步置位 (or_1_out), .in_1(8'h20), .CLK(CLK), .Q(time1));  // open: cout
  \红绿灯状态机  \u_红绿灯状态机_1  (
    .S0(STATUS[2]), .R1(R1), .S1(STATUS[1]), .S2(STATUS[0]), .Y1(Y1), .stop(not_1_out), .G1(G1), .R2(R2),
    .Y2(Y2), .G2(G2), .Pass1(Pass1), .Pass2(Pass2));
  DotMatrix #(.inputtype("column"), .matrixcols(5), .matrixrows(5), .persist(0), .dotshape("square")) dotmatrix_2 (
    .col0(LR1[24:20]), .col1(LR1[19:15]), .col2(LR1[14:10]), .col3(LR1[9:5]), .col4(LR1[4:0]));
  Comparator #(.width(8), .mode("twosComplement")) comparator_1 (.a(time1), .b(8'h4), .eq(T1));  // open: gt, lt
  Comparator #(.width(8), .mode("twosComplement")) comparator_2 (.a(time1), .b(8'h1), .eq(T2));  // open: gt, lt
  LED #(.active("true")) led_4 (.in(R2));
  LED #(.active("true")) led_5 (.in(YL2));
  LED #(.active("true")) led_6 (.in(G2));
  \双位计数器  \u_双位计数器_2  (
    .enable(\暂停 ), .mode(1'b1), .\异步置位 (or_2_out), .in_1(8'h10), .CLK(CLK), .Q(time2));  // open: cout
  or or_2 (or_2_out, RST, T2);
  \红绿灯生成函数  \u_红绿灯生成函数_1  (
    .S2(STATUS[0]), .S1(STATUS[1]), .S0(STATUS[2]), .T1(T1), .T2(T2), .T3(T3), .T4(T4), .EMERG(emerge),
    .N0(\红绿灯生成函数_1_n0 [0]), .N1(\红绿灯生成函数_1_n0 [1]), .N2(\红绿灯生成函数_1_n0 [2]));
  and and_1 (YL2, Y2, CLK);
  and and_2 (YL1, Y1, CLK);
  Comparator #(.width(8), .mode("twosComplement")) comparator_3 (.a(time2), .b(8'h4), .eq(T3));  // open: gt, lt
  Comparator #(.width(8), .mode("twosComplement")) comparator_4 (.a(time2), .b(8'h1), .eq(T4));  // open: gt, lt
  not not_2 (\暂停 , in_2);
  not not_3 (not_3_out, emerge);
  // DipSwitch #(.NSwitches(1)) dipswitch_1: pin names not known; wires that end beside it: dipswitch_1_p1
  Multiplexer #(.select(1), .width(8), .disabled("Z"), .enable("false")) multiplexer_1 (
    .in0(time1), .in1(time2), .out({Dout2, Dout1}), .sel(Pass2));
  xnor xnor_1 (xnor_1_out, R1, \暂停 );
  xnor xnor_2 (xnor_2_out, R2, \暂停 );
  Clock #(.highDuration(1), .lowDuration(1)) clock_1 (.out(CLK));
  or or_3 (emerge, E, dipswitch_1_p1);
  \左右转  \u_左右转_1  (
    .out_3(LR[4:0]), .out_5(LR[9:5]), .out_4(LR[14:10]), .out_6(LR[19:15]), .out_7(LR[24:20]), .\左转 (G1),
    .\右转 (xnor_1_out));
  \左右转  \u_左右转_2  (
    .out_3(LR1[4:0]), .out_5(LR1[9:5]), .out_4(LR1[14:10]), .out_6(LR1[19:15]), .out_7(LR1[24:20]),
    .\左转 (G2), .\右转 (xnor_2_out));
  D_Flip_Flop #(.trigger("rising"), .Pre_Clr_Positions("LEGACY"), .NegatePresetClear("false"), .enable("true"), .NewFFLayout("false")) d_ff_1 (
    .clk(CLK), .D(not_3_out), .Qn(RST));  // open: Q, preset, en, reset

  // Notes on the sheet:
  //   绿灯可以左转，红灯可以右转
endmodule

module \左右转  (
  input  \右转 ,
  input  \左转 ,
  output [4:0] out_3,
  output [4:0] out_4,
  output [4:0] out_5,
  output [4:0] out_6,
  output [4:0] out_7
);

  or or_1 (out_3[2], \右转 , \左转 );

  assign {out_4[4], out_4[2], out_4[0]} = {3{out_3[2]}};
  assign out_5[3:1] = {\右转 , out_3[2], \右转 };
  assign out_6[3:1] = {\左转 , out_3[2], \左转 };
  assign out_7[2] = out_3[2];

  // Other names for the same wires on the sheet: Din1[4:0] = {out_5[4], \右转 , out_3[2], \右转 , out_5[0]};
  //   Din2[4:0] = out_3; Din3[4:0] = {out_3[2], out_4[3], out_3[2], out_4[1], out_3[2]};
  //   Din4[4:0] = {out_6[4], \左转 , out_3[2], \左转 , out_6[0]}; Din5[4:0] = {out_7[4:3], out_3[2], out_7[1:0]}
endmodule
